# Fritzing sketch F90BMPCHPT91MH6 (saved by Fritzing 0.8.3b)
breadboards: 1

parts:
  Raspberry_Pi_rev2 = Raspberry Pi rev2
  LCD1 = LCD screen
  TR1 = Trimmer Potentiometer [package=THT]
  Součástka2 = RFID-RC522 Reader
  LED1 = LED - 5mm [color="Red (633nm)" package="5 mm [THT]"]
  R1 = Resistor [tolerance=±1% resistance=68 package=THT]
  J1 = Piezo Speaker

nets:
  3V3: Raspberry_Pi_rev2.3V3, Součástka2.3.3V
  5V: Raspberry_Pi_rev2.5V, LCD1.VDD, LCD1.LED+, TR1.leg1
  GND: Raspberry_Pi_rev2.GND, LCD1.VSS, LCD1.R/W, LCD1.LED-, TR1.leg2, Součástka2.GND, LED1.cathode, J1.pin1
  N1: Raspberry_Pi_rev2.GPIO_23, LCD1.DB4
  N2: Raspberry_Pi_rev2.GPIO_14, R1.Pin_1
  N3: Raspberry_Pi_rev2.GPIO_17, LCD1.E
  N4: Raspberry_Pi_rev2.GPIO_18, LCD1.DB7
  N5: Raspberry_Pi_rev2.GPIO_27, J1.pin2
  N6: Raspberry_Pi_rev2.GPIO_22, LCD1.RS
  N7: Raspberry_Pi_rev2.GPIO4, LCD1.DB6
  N8: Raspberry_Pi_rev2.GPIO_24, LCD1.DB5
  N9: Raspberry_Pi_rev2.GPIO_10, Součástka2.MOSI
  N10: Raspberry_Pi_rev2.GPIO_9, Součástka2.IRQ, Součástka2.MISO
  N11: Raspberry_Pi_rev2.GPIO_25, Součástka2.RST
  N12: Raspberry_Pi_rev2.GPIO_11, Součástka2.SCK
  N13: Raspberry_Pi_rev2.GPIO_8, Součástka2.SDA
  N14: LCD1.V0, TR1.wiper
  N15: LED1.anode, R1.Pin_0
